# Fritzing sketch shematic (saved by Fritzing 1.0.0rc)
breadboards: 1

parts:
  Mod1 = Amica NodeMCU DEVKIT 1.0
  HC-SR04_Sensor_1 = HC-SR04 Ultrasonic Distance Sensor
  RGB_SMD_LED1 = SMD RGB LED (WS2812) [package=5050]
  R1 = Resistor [tolerance=±5% resistance=10k package="0805 [SMD]"]
  R2 = Resistor [tolerance=±5% resistance=10k package="0805 [SMD]"]

nets:
  N1: Mod1.pin1, Mod1.pin_10, Mod1.pin_26
  N2: Mod1.pin2, Mod1.pin_9, Mod1.pin_25, Mod1.pin_29
  N3: Mod1.pin_12, RGB_SMD_LED1.DIn
  N4: Mod1.pin_13, HC-SR04_Sensor_1.TRIG
  N5: Mod1.pin_14, R1.Pin_0, R2.Pin_0
  N6: HC-SR04_Sensor_1.VCC, RGB_SMD_LED1.NC
  N7: HC-SR04_Sensor_1.ECHO, R1.Pin_1
  GND: HC-SR04_Sensor_1.GND, RGB_SMD_LED1.VSS, R2.Pin_1
